// Logisim project 4-BIT-UP COUNTER.circ as structural Verilog: 1 circuit, main circuit main
module main (
  input  clr,
  input  pre,
  input  D,
  output Q3,
  output Q2,
  output Q1,
  output Q0
);

  wire clk_out;

  Clock clk (.out(clk_out));
  D_Flip_Flop d_ff_1 (.clk(clk_out), .D(D), .Q(Q3), .preset(pre), .reset(clr));  // open: Qn, en
  D_Flip_Flop d_ff_2 (.clk(clk_out), .D(Q3), .Q(Q2), .preset(pre), .reset(clr));  // open: Qn, en
  D_Flip_Flop d_ff_3 (.clk(clk_out), .D(Q2), .Q(Q1), .preset(pre), .reset(clr));  // open: Qn, en
  D_Flip_Flop d_ff_4 (.clk(clk_out), .D(Q1), .Q(Q0), .preset(pre), .reset(clr));  // open: Qn, en
endmodule
